# Fritzing sketch fritzing (saved by Fritzing 0.9.3b)
breadboards: 1

parts:
  NANO = Arduino Nano (Rev3.0)
  U1 = 74HC595 [package="DIP16 [THT]"]
  U2 = 74HC595 [package="DIP16 [THT]"]

nets:
  GND: NANO.GND
  N1: NANO.D8, U1.DS
  N2: NANO.D11/MOSI, U1.SH_CP, U2.SH_CP
  N3: NANO.D12/MISO, U1.ST_CP, U2.ST_CP
  5V: NANO.5V, U1.VCC, U2.VCC
  N4: U1.Q7', U2.DS
